# Fritzing sketch SunriseAlarmClock (saved by Fritzing 0.9.2b)

parts:
  Encoder = ENCODER_RGB_CA [package=encoder_led_3]
  Grove1 = Grove OLED 128x96
  AC_Dimmer = mystery part, 4 pins [chip_label="AC Dimmer"]
  Bauteil2 = Arduino Nano (Rev3.0)

nets:
  N1: Encoder.-B, Bauteil2.D6
  N2: Encoder.+, Bauteil2.D5
  N3: Encoder.A, Bauteil2.D7
  VCC: Encoder.B, Grove1.VCC, AC_Dimmer.pin1, Bauteil2.3V3
  GND: Encoder.C, Grove1.GND, AC_Dimmer.pin2, Bauteil2.GND
  N4: Grove1.SDA, Bauteil2.A4
  N5: Grove1.SCL, Bauteil2.A5
  N6: AC_Dimmer.pin3, Bauteil2.D2
  N7: AC_Dimmer.pin4, Bauteil2.D4
